# Fritzing sketch LightPetSchematic (saved by Fritzing 0.9.2b)
circuit board: 8.46667cm x 5.64444cm
breadboards: 1

parts:
  U1 = NodeMCU V1.0
  U2 = SHT1x Humdity Sensor [package=sht1x]
  R1 = Resistor [tolerance=±5% resistance=10k package=THT]
  R2 = Resistor [tolerance=±5% resistance=10k package=THT]
  C1 = Ceramic Capacitor [capacitance=100nF voltage=16V package="100 mil [THT, multilayer]"]
  Part1 = Breakout Board for Electret Microphone
  U3 = 74HC4052 [package=dil16]
  TSL257 = Ambient Light Sensor (TEMT6000 Breakout Board)
  R3 = Resistor [tolerance=±5% resistance=1k package=THT]
  R4 = Resistor [tolerance=±5% resistance=10k package=THT]

nets:
  N1: U1.D1, U2.SCK, R2.Pin_1
  N2: U1.D2, U2.DATA, R1.Pin_1
  N3: U1.D3, U3.A
  N4: U1.D4, U3.B
  VCC: U1.3V3, U2.VDD, R1.Pin_0, R2.Pin_0, C1.0, Part1.VCC, U3.VCC, TSL257.VCC
  GND: U1.GND, U2.GND, C1.1, Part1.GND, U3.INH, U3.VEE, U3.GND, TSL257.GND, R4.Pin_0
  N5: U1.A0, U3.X
  N6: Part1.AUD, U3.X2
  N7: U3.X1, R3.Pin_1, R4.Pin_1
  N8: TSL257.S, R3.Pin_0

notes:
  Voltage divider used to lower light sensor voltage slightly so that it doesn't clip on the NodeMCU's analog input

custom parts:
  NodeMCU V1.0: ESP8266 based NodeMCU
